# Fritzing sketch sketch1 (saved by Fritzing 0.9.4)

parts:
  Arduino_UNO = Arduino Uno (Rev3)
  Arduino_Nano = Arduino Nano (Rev3.0)
  Tx = mystery part, 3 pins [chip_label=?]
  Rx = mystery part, 4 pins [chip_label=?]
  L298N1 = L298N DC motor driver

nets:
  N1: Arduino_UNO.D12/MISO, Tx.pin1
  N2: Arduino_UNO.GND, Tx.pin3
  N3: Arduino_UNO.5V, Tx.pin2
  N4: Arduino_Nano.D11/MOSI, Rx.pin3
  N5: Arduino_Nano.GND, Rx.pin4
  N6: Arduino_Nano.5V, Rx.pin1, L298N1.OUT3

notes:
  Transmitter
  Reciever

custom parts:
  L298N DC motor driver: 2x DC motor driver with 78M05 positive voltage regulator (7..35 V) L298N: max 46 V, 2 A Set 5 V Enable jumper to enable 5 V regultor (needed for the L298N) and +5 V output at screw terminal or supply external +5 V at screw terminal Set ENA and/or ENB to +5 V to enable motor permanently or supply ENA and/or ENB with PWM signal IN1 and IN2 set rotation directory for motor A (OUT1/OUT2) IN2 and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
